// Logisim project armazenamento_multiplos_bits.circ as structural Verilog: 3 circuits, main circuit main
module main (
  input  [4:0] in_1
);

  wire clock_1_out, n4bit_7seg_1_a, n4bit_7seg_1_b, n4bit_7seg_1_c, n4bit_7seg_1_d, n4bit_7seg_1_e,
       n4bit_7seg_1_f, n4bit_7seg_1_g, n4bit_7seg_2_a, n4bit_7seg_2_b, n4bit_7seg_2_c, n4bit_7seg_2_d,
       n4bit_7seg_2_e, n4bit_7seg_2_f, n4bit_7seg_2_g, n5bit_to_4bit_1_y0, n5bit_to_4bit_1_y1,
       n5bit_to_4bit_1_y2, n5bit_to_4bit_1_y3, n5bit_to_4bit_1_z0, n5bit_to_4bit_1_z1, n5bit_to_4bit_1_z2,
       n5bit_to_4bit_1_z3;
  wire [4:0] register_1_q;

  Clock clock_1 (.out(clock_1_out));
  Register #(.width(5), .Select("low")) register_1 (.D(in_1), .Q(register_1_q), .clk(clock_1_out));  // open: en, clr
  _5bit_to_4bit u_5bit_to_4bit_1 (
    .w(register_1_q[4]), .z0(n5bit_to_4bit_1_z0), .x(register_1_q[3]), .z1(n5bit_to_4bit_1_z1),
    .y(register_1_q[2]), .z2(n5bit_to_4bit_1_z2), .z(register_1_q[1]), .k(register_1_q[0]),
    .z3(n5bit_to_4bit_1_z3), .y0(n5bit_to_4bit_1_y0), .y1(n5bit_to_4bit_1_y1), .y2(n5bit_to_4bit_1_y2),
    .y3(n5bit_to_4bit_1_y3));
  _4bit_7seg u_4bit_7seg_1 (
    .W(n5bit_to_4bit_1_z0), .X(n5bit_to_4bit_1_z1), .Y(n5bit_to_4bit_1_z2), .Z(n5bit_to_4bit_1_z3),
    .a(n4bit_7seg_1_a), .b(n4bit_7seg_1_b), .c(n4bit_7seg_1_c), .d(n4bit_7seg_1_d), .e(n4bit_7seg_1_e),
    .f(n4bit_7seg_1_f), .g(n4bit_7seg_1_g));
  _4bit_7seg u_4bit_7seg_2 (
    .W(n5bit_to_4bit_1_y0), .X(n5bit_to_4bit_1_y1), .Y(n5bit_to_4bit_1_y2), .Z(n5bit_to_4bit_1_y3),
    .a(n4bit_7seg_2_a), .b(n4bit_7seg_2_b), .c(n4bit_7seg_2_c), .d(n4bit_7seg_2_d), .e(n4bit_7seg_2_e),
    .f(n4bit_7seg_2_f), .g(n4bit_7seg_2_g));
  _7_Segment_Display u_7_segment_display_1 (
    .g(n4bit_7seg_1_g), .f(n4bit_7seg_1_f), .a(n4bit_7seg_1_a), .b(n4bit_7seg_1_b), .e(n4bit_7seg_1_e),
    .d(n4bit_7seg_1_d), .c(n4bit_7seg_1_c));  // open: dp
  _7_Segment_Display u_7_segment_display_2 (
    .g(n4bit_7seg_2_g), .f(n4bit_7seg_2_f), .a(n4bit_7seg_2_a), .b(n4bit_7seg_2_b), .e(n4bit_7seg_2_e),
    .d(n4bit_7seg_2_d), .c(n4bit_7seg_2_c));  // open: dp
endmodule

module _5bit_to_4bit (
  input  w,
  input  x,
  input  y,
  input  z,
  input  k,
  output z0,
  output z1,
  output z2,
  output z3,
  output y0,
  output y1,
  output y2,
  output y3
);

  wire and_1_out, and_2_out, and_3_out, and_4_out, and_5_out, and_6_out, and_7_out, and_8_out, and_9_out,
       and_10_out, and_11_out, and_12_out, and_13_out, and_14_out, and_15_out, and_16_out, and_17_out,
       and_18_out, not_1_out, not_2_out, not_3_out, not_4_out, not_5_out, not_6_out, not_7_out, not_8_out,
       not_9_out, not_10_out, not_11_out, not_12_out, not_13_out, not_14_out, not_15_out, not_16_out,
       not_17_out, not_18_out, not_19_out, not_20_out, not_21_out, not_22_out, not_23_out, not_24_out,
       not_25_out;

  and and_1 (and_1_out, w, y);
  and and_2 (and_2_out, w, x);
  not not_1 (not_1_out, w);
  not not_2 (not_2_out, w);
  not not_3 (not_3_out, x);
  not not_4 (not_4_out, y);
  not not_5 (not_5_out, w);
  not not_6 (not_6_out, y);
  not not_7 (not_7_out, z);
  not not_8 (not_8_out, x);
  not not_9 (not_9_out, y);
  not not_10 (not_10_out, z);
  not not_11 (not_11_out, w);
  not not_12 (not_12_out, x);
  not not_13 (not_13_out, w);
  not not_14 (not_14_out, y);
  not not_15 (not_15_out, z);
  not not_16 (not_16_out, y);
  not not_17 (not_17_out, w);
  not not_18 (not_18_out, x);
  not not_19 (not_19_out, x);
  not not_20 (not_20_out, w);
  not not_21 (not_21_out, z);
  not not_22 (not_22_out, x);
  not not_23 (not_23_out, y);
  not not_24 (not_24_out, z);
  not not_25 (not_25_out, y);
  or or_1 (z2, and_1_out, and_2_out);
  and and_3 (and_3_out, not_1_out, x, z);
  and and_4 (and_4_out, not_2_out, x, y);
  and and_5 (and_5_out, x, y, z);
  and and_6 (and_6_out, w, not_3_out, not_4_out);
  and and_7 (and_7_out, not_5_out, x, not_6_out, not_7_out);
  and and_8 (and_8_out, w, not_8_out, not_9_out, z);
  and and_9 (and_9_out, w, x, y, not_10_out);
  and and_10 (and_10_out, not_11_out, not_12_out, y);
  and and_11 (and_11_out, not_13_out, y, z);
  and and_12 (and_12_out, w, not_14_out, not_15_out);
  and and_13 (and_13_out, w, x, not_16_out);
  and and_14 (and_14_out, not_17_out, not_18_out, z);
  and and_15 (and_15_out, not_19_out, y, z);
  and and_16 (and_16_out, not_20_out, x, y, not_21_out);
  and and_17 (and_17_out, w, not_22_out, not_23_out, not_24_out);
  and and_18 (and_18_out, w, x, not_25_out, z);
  or or_2 (z3, and_3_out, and_4_out, and_5_out, and_6_out);
  or or_3 (y0, and_7_out, and_8_out, and_9_out);
  or or_4 (y1, and_10_out, and_11_out, and_12_out, and_13_out);
  or or_5 (y2, and_14_out, and_15_out, and_16_out, and_17_out, and_18_out);

  assign y3 = k;
  assign z0 = 1'b0;
  assign z1 = 1'b0;
endmodule

module _4bit_7seg (
  input  W,
  input  X,
  input  Y,
  input  Z,
  output a,
  output b,
  output c,
  output d,
  output e,
  output f,
  output g
);

  wire and_1_out, and_2_out, and_3_out, and_4_out, and_5_out, and_6_out, and_7_out, and_8_out, and_9_out,
       and_10_out, and_11_out, and_12_out, and_13_out, and_14_out, and_15_out, and_16_out, and_17_out,
       and_18_out, and_19_out, and_20_out, and_21_out, and_22_out, and_23_out, and_24_out, and_25_out,
       and_26_out, not_1_out, not_2_out, not_3_out, not_4_out, not_5_out, not_6_out, not_7_out, not_8_out,
       not_9_out, not_10_out, not_11_out, not_12_out, not_13_out, not_14_out, not_15_out, not_16_out,
       not_17_out, not_18_out, not_19_out, not_20_out, not_21_out, not_22_out, not_23_out, not_24_out,
       not_25_out, not_26_out, not_27_out, not_28_out, not_29_out, not_30_out, not_31_out, not_32_out,
       not_33_out, not_34_out, not_35_out, not_36_out, not_37_out, not_38_out, not_39_out, not_40_out,
       not_41_out, not_42_out, not_43_out, not_44_out, not_45_out, not_46_out, not_47_out, not_48_out,
       not_49_out, not_50_out, not_51_out, not_52_out;

  not not_1 (not_1_out, W);
  not not_2 (not_2_out, X);
  and and_1 (and_1_out, not_1_out, not_2_out, not_3_out);
  not not_3 (not_3_out, Z);
  not not_4 (not_4_out, W);
  and and_2 (and_2_out, not_4_out, Y);
  not not_5 (not_5_out, W);
  and and_3 (and_3_out, not_5_out, X, Z);
  and and_4 (and_4_out, W, not_6_out, not_7_out);
  not not_6 (not_6_out, X);
  not not_7 (not_7_out, Y);
  not not_8 (not_8_out, W);
  and and_5 (and_5_out, not_8_out, not_9_out);
  not not_9 (not_9_out, X);
  not not_10 (not_10_out, W);
  and and_6 (and_6_out, not_10_out, not_11_out, not_12_out);
  not not_11 (not_11_out, Y);
  not not_12 (not_12_out, Z);
  not not_13 (not_13_out, X);
  and and_7 (and_7_out, not_13_out, not_14_out);
  not not_14 (not_14_out, Y);
  not not_15 (not_15_out, W);
  and and_8 (and_8_out, not_15_out, Y, Z);
  not not_16 (not_16_out, X);
  and and_9 (and_9_out, not_16_out, not_17_out);
  not not_17 (not_17_out, Y);
  not not_18 (not_18_out, W);
  and and_10 (and_10_out, not_18_out, Z);
  not not_19 (not_19_out, W);
  and and_11 (and_11_out, not_19_out, X);
  not not_20 (not_20_out, W);
  not not_21 (not_21_out, X);
  not not_22 (not_22_out, Z);
  not not_23 (not_23_out, W);
  not not_24 (not_24_out, X);
  not not_25 (not_25_out, W);
  not not_26 (not_26_out, Z);
  not not_27 (not_27_out, W);
  not not_28 (not_28_out, Y);
  not not_29 (not_29_out, X);
  not not_30 (not_30_out, Y);
  not not_31 (not_31_out, X);
  not not_32 (not_32_out, Y);
  and and_12 (and_12_out, not_31_out, not_32_out, not_33_out);
  not not_33 (not_33_out, Z);
  not not_34 (not_34_out, W);
  and and_13 (and_13_out, not_34_out, Y, not_35_out);
  not not_35 (not_35_out, Z);
  not not_36 (not_36_out, W);
  not not_37 (not_37_out, Y);
  and and_14 (and_14_out, not_36_out, not_37_out, not_38_out);
  not not_38 (not_38_out, Z);
  not not_39 (not_39_out, W);
  and and_15 (and_15_out, not_39_out, X, not_40_out);
  not not_40 (not_40_out, Y);
  not not_41 (not_41_out, W);
  and and_16 (and_16_out, not_41_out, X, not_42_out);
  not not_42 (not_42_out, Z);
  not not_43 (not_43_out, X);
  and and_17 (and_17_out, W, not_43_out, not_44_out);
  not not_44 (not_44_out, Y);
  not not_45 (not_45_out, W);
  and and_18 (and_18_out, not_45_out, not_46_out);
  not not_46 (not_46_out, Z);
  not not_47 (not_47_out, W);
  and and_19 (and_19_out, not_47_out, not_48_out, Y);
  not not_48 (not_48_out, X);
  not not_49 (not_49_out, W);
  and and_20 (and_20_out, not_49_out, X, not_50_out);
  not not_50 (not_50_out, Y);
  not not_51 (not_51_out, X);
  and and_21 (and_21_out, W, not_51_out, not_52_out);
  not not_52 (not_52_out, Y);
  or or_1 (a, and_1_out, and_2_out, and_3_out, and_4_out);
  or or_2 (b, and_5_out, and_6_out, and_7_out, and_8_out);
  or or_3 (c, and_9_out, and_10_out, and_11_out);
  and and_22 (and_22_out, not_20_out, not_21_out, not_22_out);
  and and_23 (and_23_out, not_23_out, not_24_out, Y);
  and and_24 (and_24_out, not_25_out, Y, not_26_out);
  and and_25 (and_25_out, not_27_out, X, not_28_out, Z);
  and and_26 (and_26_out, W, not_29_out, not_30_out);
  or or_4 (e, and_12_out, and_13_out);
  or or_5 (f, and_14_out, and_15_out, and_16_out, and_17_out);
  or or_6 (g, and_18_out, and_19_out, and_20_out, and_21_out);
  or or_7 (d, and_22_out, and_23_out, and_24_out, and_25_out, and_26_out);
endmodule
