// Logisim project Gerador de sequencia.circ as structural Verilog
module Gerador_de_sequencia (
  output [3:0] out_1
);

  wire and_3_out, and_4_out, clock_1_out, not_1_out, not_2_out, not_4_out, not_5_out;
  wire [0:0] register_1_q;
  wire [1:0] not_6_out;

  Clock clock_1 (.out(clock_1_out));
  Register #(.width(2), .Select("low")) register_1 (
    .D(not_6_out), .Q({out_1[3], register_1_q[0]}), .clk(clock_1_out));  // open: en, clr
  and and_1 (out_1[2], out_1[3], not_1_out);
  not not_1 (not_1_out, register_1_q[0]);
  not not_2 (not_2_out, out_1[3]);
  and and_2 (out_1[1], not_2_out, register_1_q[0]);
  not not_3 (out_1[0], out_1[3]);
  not not_4 (not_4_out, out_1[3]);
  and and_3 (and_3_out, not_4_out, register_1_q[0]);
  and and_4 (and_4_out, out_1[3], not_5_out);
  not not_5 (not_5_out, register_1_q[0]);
  not not_6 (not_6_out[0], register_1_q[0]);
  or or_1 (not_6_out[1], and_3_out, and_4_out);

  // Notes on the sheet:
  //   ALUNO: Guilherme Stein Kuhn
  //   DISCIPLINA: Sistemas Digitais
  //   DESCRIÇÃO: Circuito gerador de sequencia (0001 - 0011 - 1100 - 1000). Ex 3.10 Vahid
endmodule
