// Logisim project Chave de carro segura.circ as structural Verilog
module Chave_de_carro_segura (
  input  a,
  output r,
  output [2:0] n2n1n0
);

  wire and_1_out, and_2_out, and_3_out, and_5_out, and_6_out, and_7_out, and_8_out, clock_1_out, not_1_out,
       not_2_out, not_3_out, not_4_out, not_5_out, not_6_out, not_7_out, not_8_out, not_9_out, not_10_out,
       not_11_out, not_12_out, not_13_out, not_14_out, not_15_out;
  wire [2:0] register_1_q;

  Clock clock_1 (.out(clock_1_out));
  not not_1 (not_1_out, register_1_q[2]);
  not not_2 (not_2_out, register_1_q[1]);
  not not_3 (not_3_out, register_1_q[2]);
  not not_4 (not_4_out, register_1_q[0]);
  not not_5 (not_5_out, register_1_q[1]);
  not not_6 (not_6_out, register_1_q[0]);
  not not_7 (not_7_out, register_1_q[2]);
  not not_8 (not_8_out, register_1_q[2]);
  not not_9 (not_9_out, register_1_q[1]);
  not not_10 (not_10_out, register_1_q[2]);
  not not_11 (not_11_out, register_1_q[0]);
  not not_12 (not_12_out, register_1_q[2]);
  not not_13 (not_13_out, register_1_q[0]);
  not not_14 (not_14_out, register_1_q[2]);
  not not_15 (not_15_out, register_1_q[0]);
  Register #(.width(3), .Select("low")) register_1 (.D(n2n1n0), .Q(register_1_q), .clk(clock_1_out));  // open: en, clr
  and and_1 (and_1_out, not_1_out, not_2_out, register_1_q[0]);
  and and_2 (and_2_out, not_3_out, register_1_q[1], not_4_out);
  and and_3 (and_3_out, register_1_q[2], not_5_out, not_6_out);
  and and_4 (n2n1n0[2], not_7_out, register_1_q[1], register_1_q[0]);
  and and_5 (and_5_out, not_8_out, not_9_out, register_1_q[0]);
  and and_6 (and_6_out, not_10_out, register_1_q[1], not_11_out);
  and and_7 (and_7_out, not_12_out, not_13_out, a);
  and and_8 (and_8_out, not_14_out, register_1_q[1], not_15_out);
  or or_1 (r, and_1_out, and_2_out, and_3_out);
  or or_2 (n2n1n0[1], and_5_out, and_6_out);
  or or_3 (n2n1n0[0], and_7_out, and_8_out);
endmodule
