// Logisim project Sincronizador de aperto de botao.circ as structural Verilog
module Sincronizador_de_aperto_de_botao (
);

  wire and_1_out, and_2_out, and_4_out, bi_out, clock_1_out, not_1_out, not_2_out, not_3_out, not_4_out,
       not_5_out;
  wire [1:0] and_3_out, register_1_q;

  Button bi (.out(bi_out));
  Clock clock_1 (.out(clock_1_out));
  Register #(.width(2), .Select("low")) register_1 (
    .D(and_3_out), .Q(register_1_q), .clk(clock_1_out));  // open: en, clr
  not not_1 (not_1_out, register_1_q[1]);
  not not_2 (not_2_out, register_1_q[0]);
  not not_3 (not_3_out, register_1_q[1]);
  not not_4 (not_4_out, register_1_q[0]);
  not not_5 (not_5_out, register_1_q[1]);
  and and_1 (and_1_out, not_1_out, register_1_q[0], bi_out);
  and and_2 (and_2_out, register_1_q[1], not_2_out, bi_out);
  and and_3 (and_3_out[0], not_3_out, not_4_out, bi_out);
  and and_4 (and_4_out, not_5_out, register_1_q[0]);
  or or_1 (and_3_out[1], and_1_out, and_2_out);
  // Digital_Oscilloscope digital_oscilloscope_1: pin names not known; wires that end beside it: clock_1_out, bi_out, and_4_out

  // Notes on the sheet:
  //   ALUNO: Guilherme Stein Kuhn
  //   DISCIPLINA: Sistemas Digitais
  //   DESCRIÇÃO: Circuito sincronizador de aperto de botão. Ex 3.9 Vahid
  //   B IN
  //   B OUT
  //   CLOCK
endmodule
