// Logisim project 3.39.circ as structural Verilog: 1 circuit, main circuit main
module main (
  input  a,
  input  b,
  output y
);

  wire and_1_out, and_2_out, and_3_out, and_4_out, and_5_out, and_6_out, and_7_out, and_8_out, clock_1_out,
       not_1_out, not_2_out, not_3_out, not_4_out, not_5_out, not_6_out, not_7_out, not_8_out, not_9_out,
       not_10_out, not_11_out, not_12_out;
  wire [1:0] or_2_out, register_1_q;

  Clock clock_1 (.out(clock_1_out));
  not not_1 (not_1_out, register_1_q[0]);
  not not_2 (not_2_out, a);
  not not_3 (not_3_out, b);
  not not_4 (not_4_out, register_1_q[1]);
  not not_5 (not_5_out, register_1_q[0]);
  not not_6 (not_6_out, register_1_q[1]);
  not not_7 (not_7_out, a);
  not not_8 (not_8_out, register_1_q[1]);
  not not_9 (not_9_out, a);
  not not_10 (not_10_out, register_1_q[0]);
  not not_11 (not_11_out, register_1_q[1]);
  not not_12 (not_12_out, register_1_q[0]);
  Register #(.width(2), .Select("low")) register_1 (
    .D(or_2_out), .Q(register_1_q), .clk(clock_1_out));  // open: en, clr
  and and_1 (and_1_out, not_1_out, not_2_out, not_3_out);
  and and_2 (and_2_out, not_4_out, register_1_q[0], a);
  and and_3 (and_3_out, register_1_q[1], not_5_out);
  and and_4 (and_4_out, not_6_out, not_7_out, b);
  and and_5 (and_5_out, not_8_out, register_1_q[0], not_9_out);
  and and_6 (and_6_out, register_1_q[1], not_10_out, b);
  and and_7 (and_7_out, not_11_out, register_1_q[0]);
  and and_8 (and_8_out, register_1_q[1], not_12_out);
  or or_1 (or_2_out[1], and_1_out, and_2_out, and_3_out);
  or or_2 (or_2_out[0], and_4_out, and_5_out, and_6_out);
  or or_3 (y, and_7_out, and_8_out);
endmodule
