// Logisim project 3.40.circ as structural Verilog: 1 circuit, main circuit main
module main (
  output [2:0] X_Y_Z
);

  wire and_2_out, and_3_out, clock_1_out, not_1_out, not_2_out, not_4_out, not_5_out;
  wire [1:0] not_3_out, register_1_q;

  Clock clock_1 (.out(clock_1_out));
  not not_1 (not_1_out, register_1_q[1]);
  not not_2 (not_2_out, register_1_q[0]);
  not not_3 (not_3_out[0], register_1_q[0]);
  and and_1 (X_Y_Z[2], register_1_q[1], register_1_q[0]);
  not not_4 (not_4_out, register_1_q[0]);
  not not_5 (not_5_out, register_1_q[1]);
  Register #(.width(2), .Select("low")) register_1 (
    .D(not_3_out), .Q(register_1_q), .clk(clock_1_out));  // open: en, clr
  and and_2 (and_2_out, not_1_out, register_1_q[0]);
  and and_3 (and_3_out, register_1_q[1], not_2_out);
  and and_4 (X_Y_Z[1], register_1_q[1], not_4_out);
  and and_5 (X_Y_Z[0], not_5_out, register_1_q[0]);
  // Digital_Oscilloscope digital_oscilloscope_1: pin names not known; wires that end beside it: clock_1_out, X_Y_Z[2], X_Y_Z[1], X_Y_Z[0]
  or or_1 (not_3_out[1], and_2_out, and_3_out);
endmodule
