// Logisim project 3.44.circ as structural Verilog: 1 circuit, main circuit main
module main (
);

  wire and_1_out, and_2_out, and_3_out, and_4_out, and_5_out, and_6_out, and_7_out, and_8_out, and_9_out,
       and_10_out, clock_1_out, not_1_out, not_2_out, not_3_out, not_4_out, not_5_out, not_6_out, not_7_out,
       not_8_out, not_9_out, not_10_out, not_11_out, not_12_out, not_13_out, not_14_out, not_15_out,
       not_16_out, or_4_out, X_out, xor_1_out;
  wire [2:0] or_3_out, register_1_q;

  Button X (.out(X_out));
  not not_1 (not_1_out, register_1_q[1]);
  not not_2 (not_2_out, register_1_q[2]);
  not not_3 (not_3_out, register_1_q[0]);
  not not_4 (not_4_out, X_out);
  not not_5 (not_5_out, register_1_q[1]);
  not not_6 (not_6_out, register_1_q[2]);
  not not_7 (not_7_out, register_1_q[0]);
  not not_8 (not_8_out, register_1_q[0]);
  not not_9 (not_9_out, X_out);
  not not_10 (not_10_out, register_1_q[1]);
  not not_11 (not_11_out, register_1_q[0]);
  not not_12 (not_12_out, register_1_q[2]);
  not not_13 (not_13_out, register_1_q[0]);
  not not_14 (not_14_out, register_1_q[2]);
  not not_15 (not_15_out, register_1_q[0]);
  not not_16 (not_16_out, register_1_q[2]);
  and and_1 (and_1_out, register_1_q[2], not_1_out);
  or or_1 (or_3_out[2], and_1_out, and_2_out, and_3_out);
  and and_2 (and_2_out, not_2_out, register_1_q[1], register_1_q[0]);
  and and_3 (and_3_out, register_1_q[2], not_3_out, not_4_out);
  and and_4 (and_4_out, not_5_out, register_1_q[0]);
  or or_2 (or_3_out[1], and_4_out, and_5_out, and_6_out);
  and and_5 (and_5_out, not_6_out, register_1_q[1], not_7_out);
  and and_6 (and_6_out, register_1_q[1], not_8_out, not_9_out);
  and and_7 (and_7_out, register_1_q[2], not_10_out, not_11_out);
  and and_8 (and_8_out, not_12_out, register_1_q[1], not_13_out);
  or or_3 (or_3_out[0], and_7_out, and_8_out, and_9_out);
  and and_9 (and_9_out, not_14_out, not_15_out, X_out);
  xor xor_1 (xor_1_out, register_1_q[2], register_1_q[1]);
  or or_4 (or_4_out, xor_1_out, and_10_out);
  and and_10 (and_10_out, not_16_out, register_1_q[0]);
  Clock clock_1 (.out(clock_1_out));
  Register #(.width(3), .Select("low")) register_1 (
    .D(or_3_out), .Q(register_1_q), .clk(clock_1_out));  // open: en, clr
  // Digital_Oscilloscope #(.nState(14)) digital_oscilloscope_1: pin names not known; wires that end beside it: clock_1_out, X_out, or_4_out
endmodule
