// Logisim project 4.13.circ as structural Verilog: 1 circuit, main circuit main
module main (
  input  [7:0] in_1,
  output [7:0] out_2
);

  wire [2:0] c____b____a_p3;

  // DipSwitch #(.NSwitches(3)) c____b____a: pin names not known; wires that end beside it: c____b____a_p3[2], c____b____a_p3[1], c____b____a_p3[0]
  Adder adder_1 (.a({{5{1'b0}}, c____b____a_p3}), .b(in_1), .out(out_2), .cin(1'b0));  // open: cout
endmodule
