// Logisim project 4.20.circ as structural Verilog: 1 circuit, main circuit main
module main (
  input  [15:0] in_1,
  input  [2:0] in_2
);

  Multiplexer #(.select(3), .enable("false")) multiplexer_1 (.sel(in_2));  // open: in0, in1, in2, in3, in4, in5, in6, in7, out
  Multiplexer #(.select(3), .enable("false")) multiplexer_2 ();  // open: in0, in1, in2, in3, in4, in5, in6, in7, out, sel
endmodule
