// Logisim project 4.37.circ as structural Verilog: 2 circuits, main circuit main
module main (
  input  [3:0] in_1,
  input  set,
  input  count_down,
  input  clear,
  input  count_up,
  output [3:0] out_6
);

  wire clock_1_out;
  wire [2:0] bloco_construtivo_1_x;
  wire [3:0] adder_1_out, multiplexer_1_out, subtractor_1_out;

  bloco_construtivo bloco_construtivo_1 (
    .up(set), .down(count_down), .clear(clear), .set(count_up), .X(bloco_construtivo_1_x[0]),
    .Y(bloco_construtivo_1_x[1]), .Z(bloco_construtivo_1_x[2]));
  Multiplexer #(.select(3), .width(4), .enable("false")) multiplexer_1 (
    .in0(out_6), .in1(adder_1_out), .in2(subtractor_1_out), .in3(4'b0000), .in4(in_1), .in5(4'b0000),
    .in6(4'b0000), .in7(4'b0000), .out(multiplexer_1_out), .sel(bloco_construtivo_1_x));
  Register #(.width(4), .Select("low")) register_1 (
    .D(multiplexer_1_out), .Q(out_6), .clk(clock_1_out));  // open: en, clr
  Clock clock_1 (.out(clock_1_out));
  Subtractor #(.width(4)) subtractor_1 (.a(out_6), .b(4'b0001), .out(subtractor_1_out));  // open: bin, bout
  Adder #(.width(4)) adder_1 (.a(out_6), .b(4'b0001), .out(adder_1_out));  // open: cin, cout
endmodule

module bloco_construtivo (
  input  up,
  input  down,
  input  clear,
  input  set,
  output X,
  output Y,
  output Z
);

  wire and_2_out, and_3_out, and_4_out, and_5_out, not_1_out, not_2_out, not_3_out, not_4_out, not_5_out,
       not_6_out, not_7_out, not_8_out, not_9_out, not_10_out, not_11_out, not_12_out, not_13_out,
       not_14_out, not_15_out;

  not not_1 (not_1_out, up);
  not not_2 (not_2_out, down);
  not not_3 (not_3_out, clear);
  not not_4 (not_4_out, up);
  not not_5 (not_5_out, down);
  not not_6 (not_6_out, set);
  not not_7 (not_7_out, up);
  not not_8 (not_8_out, clear);
  not not_9 (not_9_out, set);
  not not_10 (not_10_out, up);
  not not_11 (not_11_out, down);
  not not_12 (not_12_out, set);
  not not_13 (not_13_out, down);
  not not_14 (not_14_out, clear);
  not not_15 (not_15_out, set);
  and and_1 (X, not_1_out, not_2_out, not_3_out, set);
  and and_2 (and_2_out, not_4_out, not_5_out, clear, not_6_out);
  or or_1 (Y, and_2_out, and_3_out);
  and and_3 (and_3_out, not_7_out, down, not_8_out, not_9_out);
  and and_4 (and_4_out, not_10_out, not_11_out, clear, not_12_out);
  or or_2 (Z, and_4_out, and_5_out);
  and and_5 (and_5_out, up, not_13_out, not_14_out, not_15_out);
endmodule
