// Logisim project 4.5.circ as structural Verilog: 1 circuit, main circuit main
module main (
  input  in_1,
  input  in_2,
  input  in_3,
  input  in_4,
  input  in_5,
  input  in_6,
  input  in_7,
  input  in_8,
  input  [1:0] in_9,
  output [7:0] out_10
);

  wire clock_1_out, multiplexer_1_out, multiplexer_2_out, multiplexer_3_out, multiplexer_4_out,
       multiplexer_5_out, multiplexer_6_out, multiplexer_7_out, multiplexer_8_out;

  Clock clock_1 (.out(clock_1_out));
  Multiplexer #(.select(2), .enable("false")) multiplexer_1 (
    .in0(out_10[7]), .in1(in_1), .in2(1'b0), .in3(out_10[3]), .out(multiplexer_1_out), .sel(in_9));
  Register #(.width(1), .Select("low")) q7 (.D(multiplexer_1_out), .Q(out_10[7]), .clk(clock_1_out));  // open: en, clr
  Multiplexer #(.select(2), .enable("false")) multiplexer_2 (
    .in0(out_10[6]), .in1(in_2), .in2(1'b0), .in3(out_10[2]), .out(multiplexer_2_out), .sel(in_9));
  Register #(.width(1), .Select("low")) q6 (.D(multiplexer_2_out), .Q(out_10[6]), .clk(clock_1_out));  // open: en, clr
  Multiplexer #(.select(2), .enable("false")) multiplexer_3 (
    .in0(out_10[5]), .in1(in_3), .in2(1'b0), .in3(out_10[1]), .out(multiplexer_3_out), .sel(in_9));
  Register #(.width(1), .Select("low")) q5 (.D(multiplexer_3_out), .Q(out_10[5]), .clk(clock_1_out));  // open: en, clr
  Multiplexer #(.select(2), .enable("false")) multiplexer_4 (
    .in0(out_10[4]), .in1(in_4), .in2(1'b0), .in3(out_10[0]), .out(multiplexer_4_out), .sel(in_9));
  Register #(.width(1), .Select("low")) q4 (.D(multiplexer_4_out), .Q(out_10[4]), .clk(clock_1_out));  // open: en, clr
  Multiplexer #(.select(2), .enable("false")) multiplexer_5 (
    .in0(out_10[3]), .in1(in_5), .in2(1'b0), .in3(out_10[7]), .out(multiplexer_5_out), .sel(in_9));
  Multiplexer #(.select(2), .enable("false")) multiplexer_6 (
    .in0(out_10[2]), .in1(in_6), .in2(1'b0), .in3(out_10[6]), .out(multiplexer_6_out), .sel(in_9));
  Register #(.width(1), .Select("low")) q3 (.D(multiplexer_5_out), .Q(out_10[3]), .clk(clock_1_out));  // open: en, clr
  Multiplexer #(.select(2), .enable("false")) multiplexer_7 (
    .in0(out_10[1]), .in1(in_7), .in2(1'b0), .in3(out_10[5]), .out(multiplexer_7_out), .sel(in_9));
  Register #(.width(1), .Select("low")) q2 (.D(multiplexer_6_out), .Q(out_10[2]), .clk(clock_1_out));  // open: en, clr
  Multiplexer #(.select(2), .enable("false")) multiplexer_8 (
    .in0(out_10[0]), .in1(in_8), .in2(1'b0), .in3(out_10[4]), .out(multiplexer_8_out), .sel(in_9));
  Register #(.width(1), .Select("low")) q1 (.D(multiplexer_7_out), .Q(out_10[1]), .clk(clock_1_out));  // open: en, clr
  Register #(.width(1), .Select("low")) q0 (.D(multiplexer_8_out), .Q(out_10[0]), .clk(clock_1_out));  // open: en, clr
endmodule
