// Logisim project 4.55.circ as structural Verilog: 1 circuit, main circuit main
module main (
  input  [15:0] in_1,
  output [15:0] out_2
);

  wire [15:0] multiplier_1_out, subtractor_1_out;

  Subtractor #(.width(16)) subtractor_1 (.a(in_1), .b(16'h111), .out(subtractor_1_out));  // open: bin, bout
  Multiplier #(.width(16)) multiplier_1 (.a(subtractor_1_out), .b(16'h2), .out(multiplier_1_out));  // open: cin, cout
  Adder #(.width(16)) adder_1 (.a(multiplier_1_out), .b(16'h20), .out(out_2));  // open: cin, cout

  // Notes on the sheet:
  //   K
  //   (K-273)
  //   (K-273)*2
  //   (K-273)*2 + 32
endmodule
