// Logisim project 4.60.circ as structural Verilog: 1 circuit, main circuit main
module main (
  input  [3:0] write_data,
  input  [1:0] read_reg1,
  input  [1:0] read_reg2,
  input  [1:0] write_reg,
  output [3:0] read_data1,
  output [3:0] read_data2
);

  wire and_1_out, and_2_out, and_3_out, and_4_out, clear_p1, clock_1_out, decoder_1_out0, decoder_1_out1,
       decoder_1_out2, decoder_1_out3;
  wire [3:0] register_1_q, register_2_q, register_4_q;

  Decoder #(.select(2), .enable("false")) decoder_1 (
    .out0(decoder_1_out0), .out1(decoder_1_out1), .out2(decoder_1_out2), .out3(decoder_1_out3),
    .sel(read_reg1));
  // DipSwitch #(.NSwitches(1)) clear: pin names not known; wires that end beside it: clear_p1
  and and_1 (and_1_out, decoder_1_out0, clear_p1);
  and and_2 (and_2_out, decoder_1_out1, clear_p1);
  Register #(.width(4), .Select("low")) register_1 (
    .D(write_data), .Q(register_1_q), .clk(clock_1_out), .clr(and_1_out));  // open: en
  Register #(.width(4), .Select("low")) register_2 (
    .D(write_data), .Q(register_2_q), .clk(clock_1_out), .clr(and_2_out));  // open: en
  Clock clock_1 (.out(clock_1_out));
  and and_3 (and_3_out, decoder_1_out2, clear_p1);
  and and_4 (and_4_out, decoder_1_out3, clear_p1);
  Register #(.width(4), .Select("low")) register_3 (
    .D(write_data), .Q(register_2_q), .clk(clock_1_out), .clr(and_3_out));  // open: en
  Register #(.width(4), .Select("low")) register_4 (
    .D(write_data), .Q(register_4_q), .clk(clock_1_out), .clr(and_4_out));  // open: en
  Multiplexer #(.select(2), .width(4), .enable("false")) multiplexer_1 (
    .in0(register_1_q), .in1(register_2_q), .in2(register_2_q), .in3(register_4_q), .out(read_data1),
    .sel(read_reg2));
  Multiplexer #(.select(2), .width(4), .enable("false")) multiplexer_2 (
    .in0(register_1_q), .in1(register_2_q), .in2(register_2_q), .in3(register_4_q), .out(read_data2),
    .sel(write_reg));
endmodule
