// Logisim project 4.11.circ as structural Verilog: 1 circuit, main circuit main
module main (
  input  [7:0] in_1,
  input  [7:0] in_2,
  input  [7:0] in_3,
  input  [7:0] in_4,
  output [7:0] Tmed
);

  wire adder_1_cout, adder_2_cout, adder_3_cout;
  wire [7:0] adder_1_out, adder_2_out, adder_3_out;

  Adder adder_1 (.a(in_3), .b(in_4), .out(adder_1_out), .cin(1'b0), .cout(adder_1_cout));
  Adder adder_2 (.a(in_2), .b(adder_1_out), .out(adder_2_out), .cin(adder_1_cout), .cout(adder_2_cout));
  Adder adder_3 (.a(in_1), .b(adder_2_out), .out(adder_3_out), .cin(adder_2_cout), .cout(adder_3_cout));
  Divider divider_1 (.a(adder_3_out), .b(8'h4), .out(Tmed));  // open: upper, rem
  // also tied to GND on the sheet: adder_3_cout
endmodule
