// Logisim project 4.12.circ as structural Verilog: 1 circuit, main circuit main
module main (
  input  [7:0] A,
  input  [7:0] B,
  output [7:0] C
);

  wire comparator_1_lt;

  Comparator #(.mode("unsigned")) comparator_1 (.a(A), .b(B), .lt(comparator_1_lt));  // open: gt, eq
  Multiplexer #(.width(8), .enable("false")) multiplexer_1 (.in0(B), .in1(A), .out(C), .sel(comparator_1_lt));
endmodule
