// Logisim project 4.20.circ as structural Verilog: 1 circuit, main circuit main
module main (
  input  [7:0] R,
  input  [7:0] G,
  input  [7:0] B,
  output [7:0] C,
  output [7:0] M,
  output [7:0] Y,
  output [7:0] K
);

  wire comparator_1_lt, comparator_2_lt;
  wire [7:0] multiplexer_1_out;

  Subtractor subtractor_1 (.a({8{1'b1}}), .b(R), .out(C));  // open: bin, bout
  Subtractor subtractor_2 (.a({8{1'b1}}), .b(G), .out(M));  // open: bin, bout
  Subtractor subtractor_3 (.a({8{1'b1}}), .b(B), .out(Y));  // open: bin, bout
  Comparator comparator_1 (.a(C), .b(M), .lt(comparator_1_lt));  // open: gt, eq
  Multiplexer #(.width(8), .enable("false")) multiplexer_1 (
    .in0(M), .in1(C), .out(multiplexer_1_out), .sel(comparator_1_lt));
  Multiplexer #(.width(8), .enable("false")) multiplexer_2 (.in0(Y), .in1(Y), .out(K), .sel(comparator_2_lt));
  Comparator comparator_2 (.a(multiplexer_1_out), .b(Y), .lt(comparator_2_lt));  // open: gt, eq

  // Notes on the sheet:
  //   -255
endmodule
