// Logisim project 4.22.circ as structural Verilog: 1 circuit, main circuit main
module main (
  input  x,
  input  y,
  input  z
);

  wire clock_1_out;
  wire [7:0] a_p8, adder_1_out, adder_2_out, and_1_out, b_p8, multiplexer_1_out, not_1_out, or_1_out,
       register_1_q, subtractor_1_out, xor_1_out;

  // DipSwitch #(.NSwitches(8)) a: pin names not known; wires that end beside it: a_p8[7], a_p8[6], a_p8[5], a_p8[4], a_p8[3], a_p8[2], a_p8[1], a_p8[0]
  // DipSwitch #(.NSwitches(8)) b: pin names not known; wires that end beside it: b_p8[7], b_p8[6], b_p8[5], b_p8[4], b_p8[3], b_p8[2], b_p8[1], b_p8[0]
  Adder adder_1 (.a(a_p8), .b(b_p8), .out(adder_1_out));  // open: cin, cout
  Subtractor subtractor_1 (.a(a_p8), .b(b_p8), .out(subtractor_1_out));  // open: bin, bout
  Adder adder_2 (.a(a_p8), .b(8'h1), .out(adder_2_out));  // open: cin, cout
  assign and_1_out = a_p8 & b_p8;  // AND_Gate and_1, 8 bits wide
  assign or_1_out = a_p8 | b_p8;  // OR_Gate or_1, 8 bits wide
  assign xor_1_out = a_p8 ^ b_p8;  // XOR_Gate xor_1, 8 bits wide
  assign not_1_out = ~a_p8;  // NOT_Gate not_1, 8 bits wide
  Multiplexer #(.select(3), .width(8), .enable("false")) multiplexer_1 (
    .in0(adder_1_out), .in1(subtractor_1_out), .in2(adder_2_out), .in3(a_p8), .in4(and_1_out),
    .in5(or_1_out), .in6(xor_1_out), .in7(not_1_out), .out(multiplexer_1_out), .sel({x, y, z}));
  LED led_1 (.in(register_1_q[6]));
  LED led_2 (.in(register_1_q[7]));
  LED led_3 (.in(register_1_q[4]));
  LED led_4 (.in(register_1_q[5]));
  Register #(.Select("low")) register_1 (
    .D(multiplexer_1_out), .en(1'b1), .Q(register_1_q), .clk(clock_1_out));  // open: clr
  Clock clock_1 (.out(clock_1_out));
  LED led_5 (.in(register_1_q[0]));
  LED led_6 (.in(register_1_q[2]));
  LED led_7 (.in(register_1_q[3]));
  LED led_8 (.in(register_1_q[1]));
endmodule
