// Logisim project 4.3 - historico temperaturas.circ as structural Verilog: 1 circuit, main circuit main
module main (
  input  [3:0] data,
  input  temporizador,
  output [3:0] a3a2a1a0,
  output [3:0] b3b2b1b0,
  output [3:0] c3_c2_c1c0
);

  wire clk_out;

  Clock clk (.out(clk_out));
  Register #(.width(4), .Select("low")) register_1 (
    .D(data), .en(temporizador), .Q(a3a2a1a0), .clk(clk_out));  // open: clr
  Register #(.width(4), .Select("low")) register_2 (
    .D(a3a2a1a0), .en(temporizador), .Q(b3b2b1b0), .clk(clk_out));  // open: clr
  Register #(.width(4), .Select("low")) register_3 (
    .D(b3b2b1b0), .en(temporizador), .Q(c3_c2_c1c0), .clk(clk_out));  // open: clr
endmodule
