// Logisim project 4.6 display retrovisor.circ as structural Verilog: 1 circuit, main circuit main
module main (
  input  [7:0] in_1,
  output [7:0] out_2
);

  wire clock_1_out, multiplexer_1_out, multiplexer_2_out, multiplexer_3_out, multiplexer_4_out,
       multiplexer_5_out, multiplexer_6_out, multiplexer_7_out, multiplexer_8_out;

  Clock clock_1 (.out(clock_1_out));
  Multiplexer #(.enable("false")) multiplexer_1 (.in0(1'b0), .in1(in_1[7]), .out(multiplexer_1_out), .sel(1'b1));
  Register #(.width(1), .Select("low")) register_1 (
    .D(multiplexer_1_out), .Q(out_2[7]), .clk(clock_1_out));  // open: en, clr
  Multiplexer #(.enable("false")) multiplexer_2 (.in0(1'b0), .in1(in_1[6]), .out(multiplexer_2_out), .sel(1'b1));
  Register #(.width(1), .Select("low")) register_2 (
    .D(multiplexer_2_out), .Q(out_2[6]), .clk(clock_1_out));  // open: en, clr
  Multiplexer #(.enable("false")) multiplexer_3 (.in0(1'b0), .in1(in_1[5]), .out(multiplexer_3_out), .sel(1'b1));
  Register #(.width(1), .Select("low")) register_3 (
    .D(multiplexer_3_out), .Q(out_2[5]), .clk(clock_1_out));  // open: en, clr
  Multiplexer #(.enable("false")) multiplexer_4 (.in0(1'b0), .in1(in_1[4]), .out(multiplexer_4_out), .sel(1'b1));
  Register #(.width(1), .Select("low")) register_4 (
    .D(multiplexer_4_out), .Q(out_2[4]), .clk(clock_1_out));  // open: en, clr
  Multiplexer #(.enable("false")) multiplexer_5 (.in0(1'b0), .in1(in_1[3]), .out(multiplexer_5_out), .sel(1'b1));
  Register #(.width(1), .Select("low")) register_5 (
    .D(multiplexer_5_out), .Q(out_2[3]), .clk(clock_1_out));  // open: en, clr
  Multiplexer #(.enable("false")) multiplexer_6 (.in0(1'b0), .in1(in_1[2]), .out(multiplexer_6_out), .sel(1'b1));
  Register #(.width(1), .Select("low")) register_6 (
    .D(multiplexer_6_out), .Q(out_2[2]), .clk(clock_1_out));  // open: en, clr
  Multiplexer #(.enable("false")) multiplexer_7 (.in0(1'b0), .in1(in_1[1]), .out(multiplexer_7_out), .sel(1'b1));
  Register #(.width(1), .Select("low")) register_7 (
    .D(multiplexer_7_out), .Q(out_2[1]), .clk(clock_1_out));  // open: en, clr
  Multiplexer #(.enable("false")) multiplexer_8 (.in0(1'b0), .in1(in_1[0]), .out(multiplexer_8_out), .sel(1'b1));
  Register #(.width(1), .Select("low")) register_8 (
    .D(multiplexer_8_out), .Q(out_2[0]), .clk(clock_1_out));  // open: en, clr
endmodule
