// Logisim project 4.7.circ as structural Verilog: 2 circuits, main circuit main
module main (
  input  [1:0] in_1,
  input  clr,
  input  set,
  input  ld,
  input  shl,
  output [1:0] out_6
);

  wire clock_1_out;
  wire [1:0] multiplexer_1_out;
  wire [2:0] modulo_1_s0;

  modulo modulo_1 (
    .clr(clr), .set(set), .ld(ld), .shl(shl), .s2(modulo_1_s0[2]), .s1(modulo_1_s0[1]), .s0(modulo_1_s0[0]));
  Multiplexer #(.select(3), .width(2), .enable("false")) multiplexer_1 (
    .in0(out_6), .in1(in_1), .in2(2'b00), .in3(2'b00), .in4(2'b11), .in5(out_6), .in6(out_6), .in7(out_6),
    .out(multiplexer_1_out), .sel(modulo_1_s0));
  Clock clock_1 (.out(clock_1_out));
  Register #(.width(2), .Select("low")) register_1 (
    .D(multiplexer_1_out), .Q(out_6), .clk(clock_1_out));  // open: en, clr
endmodule

module modulo (
  input  clr,
  input  set,
  input  ld,
  input  shl,
  output s2,
  output s1,
  output s0
);

  wire and_2_out, and_3_out, not_1_out, not_2_out, not_3_out, not_4_out;

  not not_1 (not_1_out, clr);
  not not_2 (not_2_out, set);
  not not_3 (not_3_out, ld);
  not not_4 (not_4_out, set);
  and and_1 (s2, not_1_out, set);
  and and_2 (and_2_out, not_2_out, not_3_out, shl);
  and and_3 (and_3_out, not_4_out, ld);
  or or_1 (s1, and_2_out, clr);
  or or_2 (s0, and_3_out, clr);
endmodule
