// Logisim project 4.8.circ as structural Verilog: 1 circuit, main circuit main
module main (
  output out_1
);

  wire a7_a6_a5_a4_a4_a3_a2_a1_a0_p1, a7_a6_a5_a4_a4_a3_a2_a1_a0_p2, a7_a6_a5_a4_a4_a3_a2_a1_a0_p3,
       a7_a6_a5_a4_a4_a3_a2_a1_a0_p4, a7_a6_a5_a4_a4_a3_a2_a1_a0_p5, a7_a6_a5_a4_a4_a3_a2_a1_a0_p6,
       a7_a6_a5_a4_a4_a3_a2_a1_a0_p7, a7_a6_a5_a4_a4_a3_a2_a1_a0_p8, a7_a6_a5_a4_a4_a3_a2_a1_a0_p9,
       a7_a6_a5_a4_a4_a3_a2_a1_a0_p10, a7_a6_a5_a4_a4_a3_a2_a1_a0_p11, adder_1_cout, adder_1_out,
       adder_2_cout, adder_2_out, adder_3_cout, adder_3_out, adder_4_cout, adder_4_out, adder_5_cout,
       adder_5_out, adder_6_cout, adder_6_out, adder_7_cout, adder_7_out, adder_8_cout, adder_8_out,
       b7_b6_b5_b4_b4_b3_b2_b1_b0_p1, b7_b6_b5_b4_b4_b3_b2_b1_b0_p2, b7_b6_b5_b4_b4_b3_b2_b1_b0_p3,
       b7_b6_b5_b4_b4_b3_b2_b1_b0_p4, b7_b6_b5_b4_b4_b3_b2_b1_b0_p5, clock_1_out, register_1_q, register_2_q,
       register_3_q, register_4_q, register_5_q, register_6_q, register_7_q;

  // DipSwitch #(.NSwitches(8)) b7_b6_b5_b4_b4_b3_b2_b1_b0: pin names not known; wires that end beside it: b7_b6_b5_b4_b4_b3_b2_b1_b0_p1, b7_b6_b5_b4_b4_b3_b2_b1_b0_p2, b7_b6_b5_b4_b4_b3_b2_b1_b0_p3, b7_b6_b5_b4_b4_b3_b2_b1_b0_p4, b7_b6_b5_b4_b4_b3_b2_b1_b0_p5
  // DipSwitch #(.NSwitches(8)) a7_a6_a5_a4_a4_a3_a2_a1_a0: pin names not known; wires that end beside it: a7_a6_a5_a4_a4_a3_a2_a1_a0_p1, a7_a6_a5_a4_a4_a3_a2_a1_a0_p2, a7_a6_a5_a4_a4_a3_a2_a1_a0_p3, a7_a6_a5_a4_a4_a3_a2_a1_a0_p4, a7_a6_a5_a4_a4_a3_a2_a1_a0_p5, a7_a6_a5_a4_a4_a3_a2_a1_a0_p6, a7_a6_a5_a4_a4_a3_a2_a1_a0_p7, a7_a6_a5_a4_a4_a3_a2_a1_a0_p8, a7_a6_a5_a4_a4_a3_a2_a1_a0_p9, a7_a6_a5_a4_a4_a3_a2_a1_a0_p10, a7_a6_a5_a4_a4_a3_a2_a1_a0_p11
  Adder #(.width(1)) adder_1 (
    .a(a7_a6_a5_a4_a4_a3_a2_a1_a0_p11), .b(a7_a6_a5_a4_a4_a3_a2_a1_a0_p5), .out(adder_1_out), .cin(1'b0),
    .cout(adder_1_cout));
  Clock clock_1 (.out(clock_1_out));
  Register #(.width(1), .Select("low")) register_1 (
    .D(adder_1_cout), .Q(register_1_q), .clk(clock_1_out), .clr(clock_1_out));  // open: en
  LED led_1 (.in(adder_1_out));
  Adder #(.width(1)) adder_2 (
    .a(a7_a6_a5_a4_a4_a3_a2_a1_a0_p10), .b(a7_a6_a5_a4_a4_a3_a2_a1_a0_p4), .out(adder_2_out),
    .cin(register_1_q), .cout(adder_2_cout));
  Register #(.width(1), .Select("low")) register_2 (
    .D(adder_2_cout), .Q(register_2_q), .clk(clock_1_out), .clr(clock_1_out));  // open: en
  Adder #(.width(1)) adder_3 (
    .a(a7_a6_a5_a4_a4_a3_a2_a1_a0_p9), .b(a7_a6_a5_a4_a4_a3_a2_a1_a0_p1), .out(adder_3_out),
    .cin(register_2_q), .cout(adder_3_cout));
  LED led_2 (.in(adder_2_out));
  Register #(.width(1), .Select("low")) register_3 (
    .D(adder_3_cout), .Q(register_3_q), .clk(clock_1_out), .clr(clock_1_out));  // open: en
  LED led_3 (.in(adder_3_out));
  Adder #(.width(1)) adder_4 (
    .a(a7_a6_a5_a4_a4_a3_a2_a1_a0_p8), .b(b7_b6_b5_b4_b4_b3_b2_b1_b0_p5), .out(adder_4_out),
    .cin(register_3_q), .cout(adder_4_cout));
  Adder #(.width(1)) adder_5 (
    .a(a7_a6_a5_a4_a4_a3_a2_a1_a0_p7), .b(b7_b6_b5_b4_b4_b3_b2_b1_b0_p4), .out(adder_5_out),
    .cin(register_4_q), .cout(adder_5_cout));
  Register #(.width(1), .Select("low")) register_4 (
    .D(adder_4_cout), .Q(register_4_q), .clk(clock_1_out), .clr(clock_1_out));  // open: en
  LED led_4 (.in(adder_4_out));
  Register #(.width(1), .Select("low")) register_5 (
    .D(adder_5_cout), .Q(register_5_q), .clk(clock_1_out), .clr(clock_1_out));  // open: en
  LED led_5 (.in(adder_5_out));
  Adder #(.width(1)) adder_6 (
    .a(a7_a6_a5_a4_a4_a3_a2_a1_a0_p6), .b(b7_b6_b5_b4_b4_b3_b2_b1_b0_p3), .out(adder_6_out),
    .cin(register_5_q), .cout(adder_6_cout));
  Register #(.width(1), .Select("low")) register_6 (
    .D(adder_6_cout), .Q(register_6_q), .clk(clock_1_out), .clr(clock_1_out));  // open: en
  LED led_6 (.in(adder_6_out));
  Adder #(.width(1)) adder_7 (
    .a(a7_a6_a5_a4_a4_a3_a2_a1_a0_p3), .b(b7_b6_b5_b4_b4_b3_b2_b1_b0_p2), .out(adder_7_out),
    .cin(register_6_q), .cout(adder_7_cout));
  Register #(.width(1), .Select("low")) register_7 (
    .D(adder_7_cout), .Q(register_7_q), .clk(clock_1_out), .clr(clock_1_out));  // open: en
  LED led_7 (.in(adder_7_out));
  Adder #(.width(1)) adder_8 (
    .a(a7_a6_a5_a4_a4_a3_a2_a1_a0_p2), .b(b7_b6_b5_b4_b4_b3_b2_b1_b0_p1), .out(adder_8_out),
    .cin(register_7_q), .cout(adder_8_cout));
  Register #(.width(1), .Select("low")) register_8 (.D(adder_8_cout), .Q(out_1), .clk(clock_1_out));  // open: en, clr
  LED led_8 (.in(adder_8_out));
endmodule
